// Logisim project test.circ as structural Verilog: 1 circuit, main circuit main
module main (
  input  in_1,
  input  in_2
);

  wire [31:0] adder_1_out, multiplexer_1_out, register_1_q, register_2_q;

  Multiplexer #(.enable("false"), .width(32)) multiplexer_1 (
    .in0(adder_1_out), .in1(32'h1), .out(multiplexer_1_out), .sel(in_1));
  Register #(.width(32)) register_1 (.D(multiplexer_1_out), .clk(in_2), .Q(register_1_q));  // open: en, clr
  Register #(.width(32)) register_2 (.D(register_1_q), .clk(in_2), .Q(register_2_q));  // open: en, clr
  Adder #(.width(32)) adder_1 (.a(register_1_q), .b(register_2_q), .out(adder_1_out));  // open: cin, cout
  Hex_Digit_Display hex_digit_display_1 (.value(adder_1_out[3:0]));  // open: dp
  Hex_Digit_Display hex_digit_display_2 (.value(adder_1_out[7:4]));  // open: dp
  Hex_Digit_Display hex_digit_display_3 (.value(adder_1_out[11:8]));  // open: dp
  Hex_Digit_Display hex_digit_display_4 (.value(adder_1_out[15:12]));  // open: dp
  Hex_Digit_Display hex_digit_display_5 (.value(adder_1_out[19:16]));  // open: dp
  Hex_Digit_Display hex_digit_display_6 (.value(adder_1_out[23:20]));  // open: dp
  Hex_Digit_Display hex_digit_display_7 (.value(adder_1_out[27:24]));  // open: dp
  Hex_Digit_Display hex_digit_display_8 (.value(adder_1_out[31:28]));  // open: dp
endmodule
